// Logisim project lab5.circ as structural Verilog: 1 circuit, main circuit main
module main (
  input  in_1,
  input  in_2,
  input  in_3,
  input  in_4,
  input  in_5,
  output out_6,
  output out_7,
  output out_8
);

  wire nand_2_out, nand_3_out, nand_5_out, nand_6_out;

  not nand_1 (out_6, in_1);  // NAND_Gate
  nand nand_2 (nand_2_out, in_2, in_3);
  nand nand_3 (nand_3_out, in_4, in_5);
  nand nand_4 (out_7, nand_2_out, nand_2_out);
  nand nand_5 (nand_5_out, in_4, nand_3_out);
  nand nand_6 (nand_6_out, nand_3_out, in_5);
  nand nand_7 (out_8, nand_5_out, nand_6_out);
endmodule
