// Logisim project lab7.circ as structural Verilog: 1 circuit, main circuit main
module main (
  input  X,
  input  Y,
  input  Z,
  input  W
);

  wire and_1_out, and_2_out, and_3_out, and_4_out, and_5_out, and_6_out, and_7_out, and_9_out, and_10_out,
       and_11_out, and_12_out, and_13_out, and_14_out, and_15_out, and_16_out, not_1_out, not_2_out,
       not_3_out, not_4_out;

  not not_1 (not_1_out, X);
  not not_2 (not_2_out, Y);
  not not_3 (not_3_out, Z);
  not not_4 (not_4_out, W);
  and and_1 (and_1_out, Y, W);
  // OR_Gate a has open pins: in0=X, in1=Z, in2=and_1_out, in3=and_2_out, out=open
  and and_2 (and_2_out, not_2_out, not_4_out);
  and and_3 (and_3_out, not_3_out, not_4_out);
  // OR_Gate b has open pins: in0=not_2_out, in1=and_3_out, in2=and_4_out, out=open
  and and_4 (and_4_out, Z, W);
  // OR_Gate c has open pins: in0=Y, in1=not_3_out, in2=W, out=open
  and and_5 (and_5_out, not_2_out, not_4_out);
  and and_6 (and_6_out, Z, not_4_out);
  and and_7 (and_7_out, Y, not_3_out, W);
  // OR_Gate d has open pins: in0=and_5_out, in1=and_6_out, in2=and_7_out, in3=X, in4=X, out=open
  and and_8 (X, not_2_out, Z);
  and and_9 (and_9_out, not_2_out, not_4_out);
  and and_10 (and_10_out, Z, not_4_out);
  // OR_Gate e has open pins: in0=and_9_out, in1=and_10_out, out=open
  and and_11 (and_11_out, not_3_out, not_4_out);
  // OR_Gate f has open pins: in0=X, in1=and_11_out, in2=and_12_out, in3=and_13_out, out=open
  and and_12 (and_12_out, Y, not_3_out);
  and and_13 (and_13_out, Y, not_4_out);
  and and_14 (and_14_out, Y, not_3_out);
  // OR_Gate g has open pins: in0=X, in1=and_14_out, in2=and_15_out, in3=and_16_out, out=open
  and and_15 (and_15_out, not_2_out, Z);
  and and_16 (and_16_out, Z, not_4_out);
endmodule
